# Fritzing sketch Schematic diagram (saved by Fritzing 0.9.2b)
breadboards: 2

parts:
  DI7 = 7-Segment 2 digit LED Display [package=THT]
  Часть1 = Arduino Mega 2560 (Rev3)
  U1 = 74HC595 [package="DIP16 [THT]"]
  U2 = 74HC595 [package="DIP16 [THT]"]
  S1 = Pushbutton [package="[THT]"]
  S2 = Pushbutton [package="[THT]"]
  J1 = Piezo Speaker
  LD1 = LD
  R1 = Photocell (LDR) [package=THT]
  DI8 = 7-Segment 2 digit LED Display [package=THT]
  U3 = 74HC595 [package="DIP16 [THT]"]
  U4 = 74HC595 [package="DIP16 [THT]"]
  S3 = Pushbutton [package="[THT]"]
  S4 = Pushbutton [package="[THT]"]
  R2 = Resistor [tolerance=±5% resistance=330 package=THT]
  R3 = Resistor [tolerance=±5% resistance=330 package=THT]
  R4 = Resistor [tolerance=±5% resistance=330 package=THT]
  R5 = Resistor [tolerance=±5% resistance=330 package=THT]
  R6 = Resistor [tolerance=±5% resistance=330 package=THT]
  R7 = Resistor [tolerance=±5% resistance=330 package=THT]
  R8 = Resistor [tolerance=±5% resistance=330 package=THT]
  R9 = Resistor [tolerance=±5% resistance=330 package=THT]
  R10 = Resistor [tolerance=±5% resistance=330 package=THT]
  R11 = Resistor [tolerance=±5% resistance=330 package=THT]
  R12 = Resistor [tolerance=±5% resistance=330 package=THT]
  R13 = Resistor [tolerance=±5% resistance=330 package=THT]
  R14 = Resistor [tolerance=±5% resistance=330 package=THT]
  R15 = Resistor [tolerance=±5% resistance=330 package=THT]
  R16 = Resistor [tolerance=±5% resistance=330 package=THT]
  R17 = Resistor [tolerance=±5% resistance=330 package=THT]
  R18 = Resistor [tolerance=±5% resistance=10k package=THT]
  R19 = Resistor [tolerance=±5% resistance=220 package=THT]
  R20 = Resistor [tolerance=±5% resistance=10k package=THT]
  R21 = Resistor [tolerance=±5% resistance=10k package=THT]
  R22 = Resistor [tolerance=±5% resistance=10k package=THT]
  R23 = Resistor [tolerance=±5% resistance=10k package=THT]
  R24 = Resistor [tolerance=±5% resistance=330 package=THT]
  R25 = Resistor [tolerance=±5% resistance=330 package=THT]
  R26 = Resistor [tolerance=±5% resistance=330 package=THT]
  R27 = Resistor [tolerance=±5% resistance=330 package=THT]
  R28 = Resistor [tolerance=±5% resistance=330 package=THT]
  R29 = Resistor [tolerance=±5% resistance=330 package=THT]
  R30 = Resistor [tolerance=±5% resistance=330 package=THT]
  R31 = Resistor [tolerance=±5% resistance=330 package=THT]
  R32 = Resistor [tolerance=±5% resistance=330 package=THT]
  R33 = Resistor [tolerance=±5% resistance=330 package=THT]
  R34 = Resistor [tolerance=±5% resistance=330 package=THT]
  R35 = Resistor [tolerance=±5% resistance=330 package=THT]
  R36 = Resistor [tolerance=±5% resistance=330 package=THT]
  R37 = Resistor [tolerance=±5% resistance=330 package=THT]
  R38 = Resistor [tolerance=±5% resistance=330 package=THT]
  R39 = Resistor [tolerance=±5% resistance=330 package=THT]
  R40 = Photocell (LDR) [package=THT]
  R41 = Resistor [tolerance=±5% resistance=10k package=THT]
  LD2 = LD
  R42 = Resistor [tolerance=±5% resistance=220 package=THT]  # not connected
  J2 = Piezo Speaker
  DI9 = 7-Segment 2 digit LED Display [package=THT]  # not connected
  J3 = Piezo Speaker  # not connected
  R43 = Resistor [tolerance=±5% resistance=330 package=THT]  # not connected
  R44 = Resistor [tolerance=±5% resistance=10k package=THT]  # not connected
  R45 = Resistor [tolerance=±5% resistance=220 package=THT]  # not connected

nets:
  N1: DI7.E1, R7.Pin_1
  N2: DI7.D1, R8.Pin_1
  N3: DI7.C1, R9.Pin_1
  N4: DI7.E2, R10.Pin_0
  N5: DI7.D2, R11.Pin_0
  N6: DI7.G2, R12.Pin_0
  N7: DI7.C2, R13.Pin_0
  N8: DI7.B2, R17.Pin_1
  N9: DI7.A2, R16.Pin_0
  N10: DI7.F2, R15.Pin_1
  N11: DI7.CommonCathode2, R14.Pin_1
  N12: DI7.CommonCathode1, R4.Pin_1
  N13: DI7.B1, R3.Pin_1
  N14: DI7.A1, R2.Pin_1
  N15: DI7.G1, R5.Pin_1
  N16: DI7.F1, R6.Pin_1
  N17: Часть1.A0, R1.pin_0, R18.Pin_1
  N18: Часть1.A1, R40.pin_0, R41.Pin_1
  GND: Часть1.GND, U1.GND, U1.OE, U2.GND, U2.OE, S1.Pin_1, S1.Pin_2, S2.Pin_1, S2.Pin_2, J1.pin1, R1.pin_1, U3.GND, U4.GND, U4.OE, S3.Pin_1, S3.Pin_2, S4.Pin_1, S4.Pin_2, R18.Pin_0, R20.Pin_1, R21.Pin_1, R22.Pin_1, R23.Pin_1, R41.Pin_0, LD2.cathode, J2.pin1
  N19: Часть1.D13_PWM, J2.pin2
  N20: Часть1.D12_PWM, J1.pin2
  N21: Часть1.D11_PWM, S4.Pin_3, S4.Pin_4, R23.Pin_0
  N22: Часть1.D10_PWM, S3.Pin_3, S3.Pin_4, R22.Pin_0
  N23: Часть1.D9_PWM, U3.SH_CP
  N24: Часть1.D8_PWM, U3.ST_CP
  VCC: Часть1.5V, U1.MR, U1.VCC, U2.MR, U2.VCC, U3.MR, U3.OE, U3.VCC, U4.MR, U4.VCC, R19.Pin_0, R40.pin_1
  N25: Часть1.D2_PWM, U1.DS
  N26: Часть1.D3_PWM, U1.ST_CP, U2.ST_CP
  N27: Часть1.D4_PWM, U1.SH_CP, U2.SH_CP
  N28: Часть1.D5_PWM, S1.Pin_3, S1.Pin_4, R20.Pin_0
  N29: Часть1.D6_PWM, S2.Pin_3, S2.Pin_4, R21.Pin_0
  N30: Часть1.D7_PWM, U3.DS
  N31: U1.Q1, R3.Pin_0
  N32: U1.Q2, R9.Pin_0
  N33: U1.Q3, R8.Pin_0
  N34: U1.Q4, R7.Pin_0
  N35: U1.Q5, R6.Pin_0
  N36: U1.Q6, R5.Pin_0
  N37: U1.Q7, R4.Pin_0
  N38: U1.Q7', U2.DS
  N39: U1.Q0, R2.Pin_0
  N40: U2.Q1, R17.Pin_0
  N41: U2.Q2, R13.Pin_1
  N42: U2.Q3, R11.Pin_1
  N43: U2.Q4, R10.Pin_1
  N44: U2.Q5, R15.Pin_0
  N45: U2.Q6, R12.Pin_1
  N46: U2.Q7, R14.Pin_0
  N47: U2.Q0, R16.Pin_1
  N48: LD1.anode, R19.Pin_1
  N49: DI8.E1, R33.Pin_1
  N50: DI8.D1, R34.Pin_1
  N51: DI8.C1, R35.Pin_1
  N52: DI8.E2, R36.Pin_0
  N53: DI8.D2, R37.Pin_0
  N54: DI8.G2, R38.Pin_0
  N55: DI8.C2, R39.Pin_0
  N56: DI8.B2, R32.Pin_1
  N57: DI8.A2, R31.Pin_0
  N58: DI8.F2, R30.Pin_1
  N59: DI8.CommonCathode2, R29.Pin_1
  N60: DI8.CommonCathode1, R26.Pin_1
  N61: DI8.B1, R25.Pin_1
  N62: DI8.A1, R24.Pin_1
  N63: DI8.G1, R27.Pin_1
  N64: DI8.F1, R28.Pin_1
  N65: U3.Q1, R25.Pin_0
  N66: U3.Q2, R35.Pin_0
  N67: U3.Q3, R34.Pin_0
  N68: U3.Q4, R33.Pin_0
  N69: U3.Q5, R28.Pin_0
  N70: U3.Q6, R27.Pin_0
  N71: U3.Q7, R26.Pin_0
  N72: U3.Q7', U4.DS
  N73: U3.Q0, R24.Pin_0
  N74: U4.Q1, R32.Pin_0
  N75: U4.Q2, R39.Pin_1
  N76: U4.Q3, R37.Pin_1
  N77: U4.Q4, R36.Pin_1
  N78: U4.Q5, R30.Pin_0
  N79: U4.Q6, R38.Pin_1
  N80: U4.Q7, R29.Pin_0
  N81: U4.Q0, R31.Pin_1

notes:
  DC56 - 11EWA
  Piezo Buzzer
  Resistor 10 kOm
  Resistor 330 Om
  Resistor 220 Om
  THE BALL DETECTOR
  Laser LED
  Photoresistive cell
  Increase Score
  Decrease
  Score
  Reset Score
  by pressing buttons together

custom parts:
  LD: A Generic Red Dot Laser Diode Module (~5mW)
