# Fritzing sketch Schematic diagram_v2 (saved by Fritzing 0.9.2b)

parts:
  Часть1 = Arduino Mega 2560 (Rev3)
  LD1 = LD
  R1 = Photocell (LDR) [package=THT]
  R18 = Resistor [tolerance=±5% resistance=10k package=THT]  # not connected
  R19 = Resistor [tolerance=±5% resistance=220 package=THT]
  R40 = Photocell (LDR) [package=THT]
  R41 = Resistor [tolerance=±5% resistance=10k package=THT]  # not connected
  LD2 = LD  # not connected
  R42 = Resistor [tolerance=±5% resistance=220 package=THT]  # not connected
  R44 = Resistor [tolerance=±5% resistance=10k package=THT]  # not connected
  R45 = Resistor [tolerance=±5% resistance=220 package=THT]  # not connected

nets:
  N1: Часть1.A0, R1.pin_0
  N2: Часть1.A1, R40.pin_0
  N3: Часть1.GND, LD1.cathode
  N4: LD1.anode, R19.Pin_1

notes:
  Resistor 10 kOm
  Resistor 220 Om
  THE BALL DETECTOR
  Laser LED
  Photoresistive cell

custom parts:
  LD: A Generic Red Dot Laser Diode Module (~5mW)
